# Fritzing sketch ArduinoBLDC-Controller (saved by Fritzing 0.9.3b)
breadboards: 1

parts:
  920KV_Motor1 = DJI 920 KV Motor
  Bauteil1 = Arduino Nano (Rev3.0)
  BAT1 = BC9VPC [package=bc9vpc]
  IC1 = L293D [package=THT]
  R1 = Resistor [tolerance=±0.5% resistance=1k package=THT]
  R2 = Resistor [tolerance=±0.5% resistance=1k package=THT]

nets:
  N1: 920KV_Motor1.w, IC1.Out_1_(_Controlled_by_Enable_1_)
  N2: 920KV_Motor1.v, IC1.Out_2_(_Controlled_by_Enable_1_)
  N3: Bauteil1.GND, BAT1.V-, IC1.0V
  N4: Bauteil1.D9, IC1.In_2
  N5: Bauteil1.D10, IC1.In_1
  N6: Bauteil1.D11/MOSI, IC1.In_4
  N7: Bauteil1.VIN, BAT1.V+, IC1.+Vmotor
  N8: Bauteil1.5V, IC1.+V, R1.Pin_0, R2.Pin_1
  N9: IC1.Enable_1, R1.Pin_1
  N10: IC1.Enable_2, R2.Pin_0

custom parts:
  DJI 920 KV Motor: DJI Brushless Outrunner 2212/920K Motor F330-550
