// Logisim project Logisim-CPU-Memory.circ as structural Verilog
module NAND__AND_NOT (
  input  X,
  input  Y,
  output Z
);

  wire AND_out;

  not not_1 (Z, AND_out);
  and AND (AND_out, X, Y);
endmodule

module NOT__NAND (
  input  X,
  output out_2
);

  NAND__AND_NOT nand_and_not_1 (.X(X), .Y(X), .Z(out_2));

  // Notes on the sheet:
  //   NAND
endmodule

module AND__NAND (
  input  X,
  input  Y,
  output NOT
);

  wire nand_and_not_1_z;

  NAND__AND_NOT nand_and_not_1 (.X(X), .Y(Y), .Z(nand_and_not_1_z));
  NOT__NAND not_nand_1 (.X(nand_and_not_1_z), .out_2(NOT));

  // Notes on the sheet:
  //   NAND
endmodule

module OR__NAND (
  input  X,
  input  Y,
  output Z
);

  wire not_nand_1_out_2, not_nand_2_out_2;

  NOT__NAND not_nand_1 (.X(X), .out_2(not_nand_1_out_2));
  NOT__NAND not_nand_2 (.X(Y), .out_2(not_nand_2_out_2));
  NAND__AND_NOT nand_and_not_1 (.X(not_nand_1_out_2), .Y(not_nand_2_out_2), .Z(Z));

  // Notes on the sheet:
  //   OR
endmodule

module XOR__NAND (
  input  in_1,
  input  NOT,
  output Z
);

  wire and_nand_1_not, and_nand_2_not, not_nand_1_out_2, not_nand_2_out_2;

  NOT__NAND not_nand_1 (.X(NOT), .out_2(not_nand_1_out_2));
  NOT__NAND not_nand_2 (.X(in_1), .out_2(not_nand_2_out_2));
  AND__NAND and_nand_1 (.X(in_1), .Y(not_nand_1_out_2), .NOT(and_nand_1_not));
  AND__NAND and_nand_2 (.X(not_nand_2_out_2), .Y(NOT), .NOT(and_nand_2_not));
  OR__NAND or_nand_1 (.X(and_nand_1_not), .Y(and_nand_2_not), .Z(Z));

  // Notes on the sheet:
  //   NOT
  //   AND
  //   AND
  //   OR
endmodule

module Halbaddierer (
  input  X,
  input  Y,
  output Z,
  output \Ü 
);

  XOR__NAND xor_nand_1 (.in_1(X), .NOT(Y), .Z(Z));
  AND__NAND and_nand_1 (.X(Y), .Y(X), .NOT(\Ü ));

  // Notes on the sheet:
  //   Halbaddierer
  //   XOR
  //   AND
endmodule

module Volladdierer__NAND (
  input  X,
  input  Y,
  input  \Ü0 ,
  output Z,
  output \Ü 
);

  wire halbaddierer_1_z, \halbaddierer_1_ü , \halbaddierer_2_ü ;

  Halbaddierer halbaddierer_1 (.X(X), .Y(Y), .Z(halbaddierer_1_z), .\Ü (\halbaddierer_1_ü ));
  Halbaddierer halbaddierer_2 (.X(halbaddierer_1_z), .Y(\Ü0 ), .Z(Z), .\Ü (\halbaddierer_2_ü ));
  OR__NAND or_nand_1 (.X(\halbaddierer_2_ü ), .Y(\halbaddierer_1_ü ), .Z(\Ü ));

  // Notes on the sheet:
  //   HA
  //   Volladdierer
  //   HA
  //   OR
endmodule

module _4_Bit_Addierer__NAND (
  input  A3,
  input  A2,
  input  A1,
  input  A0,
  input  B3,
  input  B2,
  input  B1,
  input  B0,
  input  \Ü0 ,
  output F0,
  output F1,
  output F2,
  output F3,
  output U__overflow
);

  wire \volladdierer_nand_1_ü , \volladdierer_nand_2_ü , \volladdierer_nand_3_ü ;

  Volladdierer__NAND volladdierer_nand_1 (.X(A0), .Y(B0), .\Ü0 (\Ü0 ), .Z(F0), .\Ü (\volladdierer_nand_1_ü ));
  Volladdierer__NAND volladdierer_nand_2 (
    .X(A1), .Y(B1), .\Ü0 (\volladdierer_nand_1_ü ), .Z(F1), .\Ü (\volladdierer_nand_2_ü ));
  Volladdierer__NAND volladdierer_nand_3 (
    .X(A2), .Y(B2), .\Ü0 (\volladdierer_nand_2_ü ), .Z(F2), .\Ü (\volladdierer_nand_3_ü ));
  Volladdierer__NAND volladdierer_nand_4 (.X(A3), .Y(B3), .\Ü0 (\volladdierer_nand_3_ü ), .Z(F3), .\Ü (U__overflow));

  // Notes on the sheet:
  //   A
  //   +
  //   B
  //   VA
  //   =
  //   F
  //   VA
  //   VA
  //   VA
endmodule

module ALU__NAND (
  input  S3,
  input  S2,
  input  S1,
  input  S0,
  input  C0,
  input  A3,
  input  A2,
  input  A1,
  input  A0,
  input  B3,
  input  B2,
  input  B1,
  input  B0,
  output F3,
  output F2,
  output F1,
  output F0,
  output C
);

  wire and_nand_1_not, and_nand_2_not, and_nand_3_not, and_nand_4_not, and_nand_5_not, and_nand_6_not,
       and_nand_7_not, and_nand_8_not, xor_nand_1_z, xor_nand_2_z, xor_nand_3_z, xor_nand_4_z, xor_nand_5_z,
       xor_nand_6_z, xor_nand_7_z, xor_nand_8_z;

  AND__NAND and_nand_1 (.X(A3), .Y(S2), .NOT(and_nand_1_not));
  AND__NAND and_nand_2 (.X(A2), .Y(S2), .NOT(and_nand_2_not));
  AND__NAND and_nand_3 (.X(A1), .Y(S2), .NOT(and_nand_3_not));
  AND__NAND and_nand_4 (.X(A0), .Y(S2), .NOT(and_nand_4_not));
  AND__NAND and_nand_5 (.X(B3), .Y(S3), .NOT(and_nand_5_not));
  AND__NAND and_nand_6 (.X(B2), .Y(S3), .NOT(and_nand_6_not));
  AND__NAND and_nand_7 (.X(B1), .Y(S3), .NOT(and_nand_7_not));
  AND__NAND and_nand_8 (.X(B0), .Y(S3), .NOT(and_nand_8_not));
  XOR__NAND xor_nand_1 (.in_1(and_nand_1_not), .NOT(S0), .Z(xor_nand_1_z));
  XOR__NAND xor_nand_2 (.in_1(and_nand_2_not), .NOT(S0), .Z(xor_nand_2_z));
  XOR__NAND xor_nand_3 (.in_1(and_nand_3_not), .NOT(S0), .Z(xor_nand_3_z));
  XOR__NAND xor_nand_4 (.in_1(and_nand_4_not), .NOT(S0), .Z(xor_nand_4_z));
  XOR__NAND xor_nand_5 (.in_1(and_nand_5_not), .NOT(S1), .Z(xor_nand_5_z));
  XOR__NAND xor_nand_6 (.in_1(and_nand_6_not), .NOT(S1), .Z(xor_nand_6_z));
  XOR__NAND xor_nand_7 (.in_1(and_nand_7_not), .NOT(S1), .Z(xor_nand_7_z));
  XOR__NAND xor_nand_8 (.in_1(and_nand_8_not), .NOT(S1), .Z(xor_nand_8_z));
  _4_Bit_Addierer__NAND u_4_bit_addierer_nand_1 (
    .A3(xor_nand_1_z), .A2(xor_nand_2_z), .A1(xor_nand_3_z), .A0(xor_nand_4_z), .B3(xor_nand_5_z),
    .B2(xor_nand_6_z), .B1(xor_nand_7_z), .B0(xor_nand_8_z), .\Ü0 (C0), .F0(F0), .F1(F1), .F2(F2), .F3(F3),
    .U__overflow(C));

  // Notes on the sheet:
  //   AND
  //   AND
  //   AND
  //   AND
  //   AND
  //   AND
  //   AND
  //   AND
  //   XOR
  //   XOR
  //   XOR
  //   XOR
  //   XOR
  //   XOR
  //   XOR
  //   XOR
  //   4Bit Volladdierer
endmodule

module RS_Latch__NAND (
  input  S,
  input  R,
  output Q,
  output nQ
);

  NOR__NAND nor_nand_1 (.X(S), .Y(Q), .Z(nQ));
  NOR__NAND nor_nand_2 (.X(nQ), .Y(R), .Z(Q));

  // Notes on the sheet:
  //   NOR
  //   NOR
endmodule

module NOR__NAND (
  input  X,
  input  Y,
  output Z
);

  wire or_nand_1_z;

  OR__NAND or_nand_1 (.X(X), .Y(Y), .Z(or_nand_1_z));
  NOT__NAND not_nand_1 (.X(or_nand_1_z), .out_2(Z));

  // Notes on the sheet:
  //   OR
  //   NOT
endmodule

module D_Latch__NAND (
  input  D,
  input  E,
  output Q,
  output nQ
);

  wire nand_and_not_1_z, nand_and_not_2_z, not_nand_1_out_2;

  NOT__NAND not_nand_1 (.X(D), .out_2(not_nand_1_out_2));
  NAND__AND_NOT nand_and_not_1 (.X(D), .Y(E), .Z(nand_and_not_1_z));
  NAND__AND_NOT nand_and_not_2 (.X(E), .Y(not_nand_1_out_2), .Z(nand_and_not_2_z));
  NAND__AND_NOT nand_and_not_3 (.X(nand_and_not_1_z), .Y(nQ), .Z(Q));
  NAND__AND_NOT nand_and_not_4 (.X(Q), .Y(nand_and_not_2_z), .Z(nQ));

  // Notes on the sheet:
  //   NOT
  //   NAND
  //   NAND
  //   NAND
  //   NAND
endmodule

module D_FlipFlop__NAND (
  input  D,
  input  E,
  output Q
);

  wire d_latch_nand_1_nq, not_nand_1_out_2, not_nand_2_out_2;

  NOT__NAND not_nand_1 (.X(D), .out_2(not_nand_1_out_2));
  D_Latch__NAND d_latch_nand_1 (.D(not_nand_1_out_2), .E(E), .nQ(d_latch_nand_1_nq));  // open: Q
  NOT__NAND not_nand_2 (.X(E), .out_2(not_nand_2_out_2));
  D_Latch__NAND d_latch_nand_2 (.D(d_latch_nand_1_nq), .E(not_nand_2_out_2), .Q(Q));  // open: nQ

  // Notes on the sheet:
  //   NOT
  //   NOT
  //   D-Latch
  //   D-Latch
endmodule

module JK_FlipFlop__NAND (
  input  J,
  input  CLK,
  input  K,
  output Q,
  output nQ
);

  wire and_nand_1_not, and_nand_2_not, nand_and_not_1_z, nand_and_not_2_z;

  NAND__AND_NOT nand_and_not_1 (.X(Q), .Y(K), .Z(nand_and_not_1_z));
  NAND__AND_NOT nand_and_not_2 (.X(J), .Y(nQ), .Z(nand_and_not_2_z));
  AND__NAND and_nand_1 (.X(nand_and_not_1_z), .Y(J), .NOT(and_nand_1_not));
  AND__NAND and_nand_2 (.X(K), .Y(nand_and_not_2_z), .NOT(and_nand_2_not));
  RS_FlipFlop__NAND rs_flipflop_nand_1 (.S(and_nand_1_not), .R(and_nand_2_not), .CLK(CLK), .Q(Q), .nQ(nQ));

  // Notes on the sheet:
  //   NAND
  //   NAND
  //   AND
  //   RS-FlipFlop
  //   AND
endmodule

module RS_FlipFlop__NAND (
  input  S,
  input  R,
  input  CLK,
  output Q,
  output nQ
);

  wire and_nand_1_not, and_nand_2_not, and_nand_3_not, and_nand_4_not, not_nand_1_out_2, rs_latch_nand_1_nq,
       rs_latch_nand_1_q;

  NOT__NAND not_nand_1 (.X(CLK), .out_2(not_nand_1_out_2));
  // Probe on and_nand_1_not
  AND__NAND and_nand_1 (.X(S), .Y(not_nand_1_out_2), .NOT(and_nand_1_not));
  AND__NAND and_nand_2 (.X(R), .Y(not_nand_1_out_2), .NOT(and_nand_2_not));
  RS_Latch__NAND rs_latch_nand_1 (
    .S(and_nand_1_not), .R(and_nand_2_not), .Q(rs_latch_nand_1_q), .nQ(rs_latch_nand_1_nq));
  AND__NAND and_nand_3 (.X(CLK), .Y(rs_latch_nand_1_q), .NOT(and_nand_3_not));
  AND__NAND and_nand_4 (.X(rs_latch_nand_1_nq), .Y(CLK), .NOT(and_nand_4_not));
  RS_Latch__NAND rs_latch_nand_2 (.S(and_nand_3_not), .R(and_nand_4_not), .Q(Q), .nQ(nQ));

  // Notes on the sheet:
  //   NOT
  //   AND
  //   RS-Latch
  //   AND
  //   AND
  //   RS-Latch
  //   AND
endmodule

module JK_FlipFlop_RS__NAND (
  input  S,
  input  J,
  input  CLK,
  input  K,
  input  R,
  output Q,
  output nQ
);

  wire nand_3x_nand_1_z, nand_3x_nand_2_z, nand_3x_nand_3_z, nand_3x_nand_4_z, nand_and_not_1_z,
       nand_and_not_2_z, not_nand_1_out_2, not_nand_2_out_2, not_nand_3_out_2, not_nand_4_out_2;

  NOT__NAND not_nand_1 (.X(CLK), .out_2(not_nand_1_out_2));
  NOT__NAND not_nand_2 (.X(S), .out_2(not_nand_2_out_2));
  NAND_3x__NAND nand_3x_nand_1 (.X1(nQ), .X2(J), .X3(not_nand_1_out_2), .Z(nand_3x_nand_1_z));
  NAND_3x__NAND nand_3x_nand_2 (.X1(not_nand_1_out_2), .X2(K), .X3(Q), .Z(nand_3x_nand_2_z));
  NOT__NAND not_nand_3 (.X(R), .out_2(not_nand_3_out_2));
  NAND_3x__NAND nand_3x_nand_3 (
    .X1(not_nand_2_out_2), .X2(nand_3x_nand_1_z), .X3(nand_3x_nand_4_z), .Z(nand_3x_nand_3_z));
  NAND_3x__NAND nand_3x_nand_4 (
    .X1(nand_3x_nand_3_z), .X2(not_nand_3_out_2), .X3(nand_3x_nand_2_z), .Z(nand_3x_nand_4_z));
  NOT__NAND not_nand_4 (.X(not_nand_1_out_2), .out_2(not_nand_4_out_2));
  NAND__AND_NOT nand_and_not_1 (.X(not_nand_4_out_2), .Y(nand_3x_nand_3_z), .Z(nand_and_not_1_z));
  NAND__AND_NOT nand_and_not_2 (.X(not_nand_4_out_2), .Y(nand_3x_nand_4_z), .Z(nand_and_not_2_z));
  NAND_3x__NAND nand_3x_nand_5 (.X1(not_nand_2_out_2), .X2(nand_and_not_1_z), .X3(nQ), .Z(Q));
  NAND_3x__NAND nand_3x_nand_6 (.X1(Q), .X2(not_nand_3_out_2), .X3(nand_and_not_2_z), .Z(nQ));

  // Notes on the sheet:
  //   NOT
  //   NOT
  //   NAND
  //   NAND
  //   NOT
  //   NAND
  //   NAND
  //   NOT
  //   NAND
  //   NAND
  //   NAND
  //   NAND
endmodule

module AND_3x__NAND (
  input  X1,
  input  X2,
  input  X3,
  output Z
);

  wire and_nand_1_not;

  AND__NAND and_nand_1 (.X(X1), .Y(X2), .NOT(and_nand_1_not));
  AND__NAND and_nand_2 (.X(and_nand_1_not), .Y(X3), .NOT(Z));

  // Notes on the sheet:
  //   AND
  //   AND
endmodule

module NAND_3x__NAND (
  input  X1,
  input  X2,
  input  X3,
  output Z
);

  wire and_3x_nand_1_z;

  AND_3x__NAND and_3x_nand_1 (.X1(X1), .X2(X2), .X3(X3), .Z(and_3x_nand_1_z));
  NOT__NAND not_nand_1 (.X(and_3x_nand_1_z), .out_2(Z));

  // Notes on the sheet:
  //   AND
  //   NOT
endmodule

module _4_Bit_Register__JK (
  input  R,
  input  S,
  input  CLK,
  input  E3,
  input  E2,
  input  E1,
  input  E0,
  output Q3,
  output Q2,
  output Q1,
  output Q0
);

  wire not_nand_1_out_2, not_nand_2_out_2, not_nand_3_out_2, not_nand_4_out_2;

  NOT__NAND not_nand_1 (.X(E3), .out_2(not_nand_1_out_2));
  JK_FlipFlop_RS__NAND jk_flipflop_rs_nand_1 (
    .S(S), .J(E3), .CLK(CLK), .K(not_nand_1_out_2), .R(R), .Q(Q3));  // open: nQ
  JK_FlipFlop_RS__NAND jk_flipflop_rs_nand_2 (
    .S(S), .J(E2), .CLK(CLK), .K(not_nand_2_out_2), .R(R), .Q(Q2));  // open: nQ
  NOT__NAND not_nand_2 (.X(E2), .out_2(not_nand_2_out_2));
  NOT__NAND not_nand_3 (.X(E1), .out_2(not_nand_3_out_2));
  JK_FlipFlop_RS__NAND jk_flipflop_rs_nand_3 (
    .S(S), .J(E1), .CLK(CLK), .K(not_nand_3_out_2), .R(R), .Q(Q1));  // open: nQ
  NOT__NAND not_nand_4 (.X(E0), .out_2(not_nand_4_out_2));
  JK_FlipFlop_RS__NAND jk_flipflop_rs_nand_4 (
    .S(S), .J(E0), .CLK(CLK), .K(not_nand_4_out_2), .R(R), .Q(Q0));  // open: nQ

  // Notes on the sheet:
  //   NOT
  //   JK-FF-RS
  //   NOT
  //   JK-FF-RS
  //   NOT
  //   JK-FF-RS
  //   NOT
  //   JK-FF-RS
endmodule

module NAND__Transistorlogik (
  input  X,
  input  X_2,
  input  Y,
  input  Y_2,
  output out_5,
  output out_6
);

  wire transistor_2_out;

  Transistor #(.\type ("n")) transistor_1 (.in(transistor_2_out), .out(out_5), .gate(X));
  Transistor #(.\type ("n")) transistor_2 (.in(1'b0), .out(transistor_2_out), .gate(Y));
  Transistor transistor_3 (.in(1'b1), .out(out_6), .gate(Y_2));
  Transistor transistor_4 (.in(1'b1), .out(out_6), .gate(X_2));

  // Notes on the sheet:
  //   NPN / NMOS bottom
  //   PNP / PMOS top
endmodule

module OR_3x__NAND (
  input  x1,
  input  x2,
  input  x3,
  output out_4
);

  wire or_nand_1_z;

  OR__NAND or_nand_1 (.X(x1), .Y(x2), .Z(or_nand_1_z));
  OR__NAND or_nand_2 (.X(or_nand_1_z), .Y(x3), .Z(out_4));

  // Notes on the sheet:
  //   OR
  //   OR
endmodule

module Decoder (
  input  Sl,
  input  Sr,
  input  I,
  output L,
  output M,
  output R
);

  wire and_nand_1_not, not_nand_1_out_2, not_nand_2_out_2;

  AND__NAND and_nand_1 (.X(not_nand_2_out_2), .Y(not_nand_1_out_2), .NOT(and_nand_1_not));
  NOT__NAND not_nand_1 (.X(Sr), .out_2(not_nand_1_out_2));
  NOT__NAND not_nand_2 (.X(Sl), .out_2(not_nand_2_out_2));
  AND__NAND and_nand_2 (.X(Sl), .Y(I), .NOT(L));
  AND__NAND and_nand_3 (.X(and_nand_1_not), .Y(I), .NOT(M));
  AND__NAND and_nand_4 (.X(Sr), .Y(I), .NOT(R));

  // Notes on the sheet:
  //   AND
  //   NOT
  //   NOT
  //   AND
  //   AND
  //   AND
endmodule

module _4_Bit_Shift (
  input  R,
  input  S,
  input  CLK,
  input  El,
  input  Er,
  input  Sl,
  input  Sr,
  input  E3,
  input  E2,
  input  E1,
  input  E0,
  output Q3,
  output Q2,
  output Q1,
  output Q0
);

  wire decoder_1_m, decoder_1_r, decoder_2_l, decoder_2_m, decoder_2_r, decoder_3_l, decoder_3_m,
       decoder_3_r, decoder_4_l, decoder_4_m, or_3x_nand_1_out_4, or_3x_nand_2_out_4, or_3x_nand_3_out_4,
       or_3x_nand_4_out_4;

  Decoder decoder_1 (.M(decoder_1_m), .R(decoder_1_r), .Sl(Sl), .Sr(Sr), .I(E3));  // open: L
  _4_Bit_Register__JK u_4_bit_register_jk_1 (
    .Q3(Q3), .Q2(Q2), .Q1(Q1), .Q0(Q0), .R(R), .S(S), .CLK(CLK), .E3(or_3x_nand_2_out_4),
    .E2(or_3x_nand_1_out_4), .E1(or_3x_nand_3_out_4), .E0(or_3x_nand_4_out_4));
  OR_3x__NAND or_3x_nand_1 (.x1(decoder_1_r), .x2(decoder_2_m), .x3(decoder_3_l), .out_4(or_3x_nand_1_out_4));
  OR_3x__NAND or_3x_nand_2 (.x1(El), .x2(decoder_1_m), .x3(decoder_2_l), .out_4(or_3x_nand_2_out_4));
  Decoder decoder_2 (.L(decoder_2_l), .M(decoder_2_m), .R(decoder_2_r), .Sl(Sl), .Sr(Sr), .I(E2));
  OR_3x__NAND or_3x_nand_3 (.x1(decoder_2_r), .x2(decoder_3_m), .x3(decoder_4_l), .out_4(or_3x_nand_3_out_4));
  Decoder decoder_3 (.L(decoder_3_l), .M(decoder_3_m), .R(decoder_3_r), .Sl(Sl), .Sr(Sr), .I(E1));
  OR_3x__NAND or_3x_nand_4 (.x1(decoder_3_r), .x2(decoder_4_m), .x3(Er), .out_4(or_3x_nand_4_out_4));
  Decoder decoder_4 (.L(decoder_4_l), .M(decoder_4_m), .Sl(Sl), .Sr(Sr), .I(E0));  // open: R

  // Notes on the sheet:
  //   OR
  //   OR
  //   Decoder
  //   4-Bit Register
  //   E
  //   OR
  //   Decoder
  //   OR
endmodule

module MiniCPU (
  input  R,
  input  S,
  input  CLK,
  input  El,
  input  Er,
  input  Sl,
  input  Sr,
  input  A0,
  input  A1,
  input  A2,
  input  A3,
  input  C0,
  input  S0,
  input  S1,
  input  S2,
  input  S3,
  output out_17,
  output out_18,
  output out_19,
  output out_20
);

  wire alu_nand_1_f0, alu_nand_1_f1, alu_nand_1_f2, alu_nand_1_f3;

  ALU__NAND alu_nand_1 (
    .S3(S3), .S2(S2), .S1(S1), .S0(S0), .C0(C0), .A3(A3), .A2(A2), .A1(A1), .A0(A0), .B3(out_17),
    .B2(out_18), .B1(out_19), .B0(out_20), .F3(alu_nand_1_f3), .F2(alu_nand_1_f2), .F1(alu_nand_1_f1),
    .F0(alu_nand_1_f0));  // open: C
  _4_Bit_Shift u_4_bit_shift_1 (
    .R(R), .S(S), .CLK(CLK), .El(El), .Er(Er), .Sl(Sl), .Sr(Sr), .Q3(out_17), .Q2(out_18), .Q1(out_19),
    .Q0(out_20), .E3(alu_nand_1_f3), .E2(alu_nand_1_f2), .E1(alu_nand_1_f1), .E0(alu_nand_1_f0));

  // Notes on the sheet:
  //   A
  //   ALU
  //   E
  //   F
  //   4-Bit-Shift Register
endmodule

module _1xMultiplexer (
  input  E0,
  input  E1,
  input  S,
  output A
);

  wire and_nand_1_not, and_nand_2_not, not_nand_1_out_2;

  NOT__NAND not_nand_1 (.X(S), .out_2(not_nand_1_out_2));
  AND__NAND and_nand_1 (.X(E0), .Y(S), .NOT(and_nand_1_not));
  AND__NAND and_nand_2 (.X(E1), .Y(not_nand_1_out_2), .NOT(and_nand_2_not));
  OR__NAND or_nand_1 (.X(and_nand_1_not), .Y(and_nand_2_not), .Z(A));

  // Notes on the sheet:
  //   NOT
  //   AND
  //   AND
  //   OR
endmodule

module _2xMultiplexer (
  input  S1,
  input  S0,
  input  E3,
  input  E2,
  input  E1,
  input  E0,
  output A
);

  wire n1xmultiplexer_1_a, n1xmultiplexer_2_a;

  _1xMultiplexer u_1xmultiplexer_1 (.E0(E3), .E1(E2), .S(S1), .A(n1xmultiplexer_1_a));
  _1xMultiplexer u_1xmultiplexer_2 (.E0(E1), .E1(E0), .S(S1), .A(n1xmultiplexer_2_a));
  _1xMultiplexer u_1xmultiplexer_3 (.E0(n1xmultiplexer_1_a), .E1(n1xmultiplexer_2_a), .S(S0), .A(A));

  // Notes on the sheet:
  //   1xMUX
  //   1xMUX
  //   1xMUX
endmodule

module _3xMultiplexer (
  input  S0,
  input  S1,
  input  S2,
  input  E0,
  input  E1,
  input  E2,
  input  E3,
  input  E4,
  input  E5,
  input  E6,
  input  E7,
  output A
);

  wire n2xmultiplexer_1_a, n2xmultiplexer_2_a;

  _2xMultiplexer u_2xmultiplexer_1 (.S1(S1), .S0(S2), .E3(E0), .E2(E1), .E1(E2), .E0(E3), .A(n2xmultiplexer_1_a));
  _2xMultiplexer u_2xmultiplexer_2 (.S1(S1), .S0(S2), .E3(E4), .E2(E5), .E1(E6), .E0(E7), .A(n2xmultiplexer_2_a));
  _1xMultiplexer u_1xmultiplexer_1 (.E0(n2xmultiplexer_1_a), .E1(n2xmultiplexer_2_a), .S(S0), .A(A));

  // Notes on the sheet:
  //   2xMUX
  //   2xMUX
  //   1xMUX
endmodule

module _4xMultiplexer (
  input  S0,
  input  S1,
  input  S1_2,
  input  S0_2,
  input  EF,
  input  EE,
  input  ED,
  input  EC,
  input  EB,
  input  EA,
  input  E9,
  input  E8,
  input  E7,
  input  E6,
  input  E5,
  input  E4,
  input  E3,
  input  E2,
  input  E1,
  input  E0,
  output A
);

  wire n2xmultiplexer_1_a, n2xmultiplexer_2_a, n2xmultiplexer_3_a, n2xmultiplexer_4_a;

  _2xMultiplexer u_2xmultiplexer_1 (.S1(S0_2), .S0(S1_2), .E3(EF), .E2(EE), .E1(ED), .E0(EC), .A(n2xmultiplexer_1_a));
  _2xMultiplexer u_2xmultiplexer_2 (.S1(S0_2), .S0(S1_2), .E3(EB), .E2(EA), .E1(E9), .E0(E8), .A(n2xmultiplexer_2_a));
  _2xMultiplexer u_2xmultiplexer_3 (.S1(S0_2), .S0(S1_2), .E3(E7), .E2(E6), .E1(E5), .E0(E4), .A(n2xmultiplexer_3_a));
  _2xMultiplexer u_2xmultiplexer_4 (.S1(S0_2), .S0(S1_2), .E3(E3), .E2(E2), .E1(E1), .E0(E0), .A(n2xmultiplexer_4_a));
  _2xMultiplexer u_2xmultiplexer_5 (
    .S1(S1), .S0(S0), .E3(n2xmultiplexer_1_a), .E2(n2xmultiplexer_2_a), .E1(n2xmultiplexer_3_a),
    .E0(n2xmultiplexer_4_a), .A(A));

  // Notes on the sheet:
  //   2xMUX
  //   2xMUX
  //   2xMUX
  //   2xMUX
endmodule

module _4Bit_Switch_E1E2__A (
  input  S,
  input  E1_0,
  input  E1_1,
  input  E1_2,
  input  E1_3,
  input  E2_0,
  input  E2_1,
  input  E2_2,
  input  E2_3,
  output A0,
  output A1,
  output A2,
  output A3
);

  _1xMultiplexer u_1xmultiplexer_1 (.E0(E1_0), .E1(E2_0), .S(S), .A(A0));
  _1xMultiplexer u_1xmultiplexer_2 (.E0(E1_1), .E1(E2_1), .S(S), .A(A1));
  _1xMultiplexer u_1xmultiplexer_3 (.E0(E1_2), .E1(E2_2), .S(S), .A(A2));
  _1xMultiplexer u_1xmultiplexer_4 (.E0(E1_3), .E1(E2_3), .S(S), .A(A3));

  // Notes on the sheet:
  //   1xMUX
  //   1xMUX
  //   1xMUX
  //   1xMUX
endmodule

module _1xDeMUX (
  input  E,
  input  S,
  output A1,
  output A2
);

  wire not_nand_1_out_2;

  NOT__NAND not_nand_1 (.X(S), .out_2(not_nand_1_out_2));
  AND__NAND and_nand_1 (.X(S), .Y(E), .NOT(A1));
  AND__NAND and_nand_2 (.X(E), .Y(not_nand_1_out_2), .NOT(A2));

  // Notes on the sheet:
  //   NOT
  //   AND
  //   AND
endmodule

module _4Bit_Switch_E__A1A2 (
  input  S,
  input  E1_0,
  input  E1_1,
  input  E1_2,
  input  E1_3,
  output A1_0,
  output A1_1,
  output A1_2,
  output A1_3,
  output A2_0,
  output A2_1,
  output A2_2,
  output A2_3
);

  _1xDeMUX u_1xdemux_1 (.E(E1_0), .S(S), .A1(A1_0), .A2(A2_0));
  _1xDeMUX u_1xdemux_2 (.E(E1_1), .S(S), .A1(A1_1), .A2(A2_1));
  _1xDeMUX u_1xdemux_3 (.E(E1_2), .S(S), .A1(A1_2), .A2(A2_2));
  _1xDeMUX u_1xdemux_4 (.E(E1_3), .S(S), .A1(A1_3), .A2(A2_3));

  // Notes on the sheet:
  //   1xDeMUX
  //   1xDeMUX
  //   1xDeMUX
  //   1xDeMUX
endmodule

module _2xDeMux (
  input  E,
  input  S0,
  input  S1,
  output A3,
  output A2,
  output A1,
  output A0
);

  wire n1xdemux_1_a1, n1xdemux_1_a2;

  _1xDeMUX u_1xdemux_1 (.E(E), .S(S0), .A1(n1xdemux_1_a1), .A2(n1xdemux_1_a2));
  _1xDeMUX u_1xdemux_2 (.E(n1xdemux_1_a1), .S(S1), .A1(A3), .A2(A2));
  _1xDeMUX u_1xdemux_3 (.E(n1xdemux_1_a2), .S(S1), .A1(A1), .A2(A0));

  // Notes on the sheet:
  //   1xDeMUX
  //   1xDeMUX
  //   1xDeMUX
endmodule

module _4xDeMux (
  input  S0,
  input  S1,
  input  S2,
  input  S3,
  input  E,
  output AF,
  output AE,
  output AD,
  output AC,
  output AB,
  output AA,
  output A9,
  output A8,
  output A7,
  output A6,
  output A5,
  output A4,
  output A3,
  output A2,
  output A1,
  output A0
);

  wire n2xdemux_1_a0, n2xdemux_1_a1, n2xdemux_1_a2, n2xdemux_1_a3;

  _2xDeMux u_2xdemux_1 (
    .E(E), .S0(S3), .S1(S2), .A3(n2xdemux_1_a3), .A2(n2xdemux_1_a2), .A1(n2xdemux_1_a1), .A0(n2xdemux_1_a0));
  _2xDeMux u_2xdemux_2 (.E(n2xdemux_1_a3), .S0(S1), .S1(S0), .A3(AF), .A2(AE), .A1(AD), .A0(AC));
  _2xDeMux u_2xdemux_3 (.E(n2xdemux_1_a2), .S0(S1), .S1(S0), .A3(AB), .A2(AA), .A1(A9), .A0(A8));
  _2xDeMux u_2xdemux_4 (.E(n2xdemux_1_a1), .S0(S1), .S1(S0), .A3(A7), .A2(A6), .A1(A5), .A0(A4));
  _2xDeMux u_2xdemux_5 (.E(n2xdemux_1_a0), .S0(S1), .S1(S0), .A3(A3), .A2(A2), .A1(A1), .A0(A0));

  // Notes on the sheet:
  //   2xDeMUX
  //   2xDeMUX
  //   2xDeMUX
  //   2xDeMUX
  //   2xDeMUX
endmodule

module _4x4Bit_RAM (
  input  R,
  input  S,
  input  E0,
  input  E1,
  input  E2,
  input  E3,
  input  W,
  input  A1,
  input  A0,
  output O3,
  output O2,
  output O1,
  output O0
);

  wire _2xDeMux_a0, _2xDeMux_a1, _2xDeMux_a2, _2xDeMux_a3, _4_Bit_Register_2_q0, _4_Bit_Register_2_q1,
       _4_Bit_Register_2_q2, _4_Bit_Register_2_q3, _4_Bit_Register_3_q0, _4_Bit_Register_3_q1,
       _4_Bit_Register_3_q2, _4_Bit_Register_3_q3, _4_Bit_Register_4_q0, _4_Bit_Register_4_q1,
       _4_Bit_Register_4_q2, _4_Bit_Register_4_q3, _4_Bit_Register_q0, _4_Bit_Register_q1,
       _4_Bit_Register_q2, _4_Bit_Register_q3, _4Bit_Switch_3_a0, _4Bit_Switch_3_a1, _4Bit_Switch_3_a2,
       _4Bit_Switch_3_a3, _4Bit_Switch_a0, _4Bit_Switch_a1, _4Bit_Switch_a2, _4Bit_Switch_a3;

  _4_Bit_Register__JK _4_Bit_Register (
    .Q3(_4_Bit_Register_q3), .Q2(_4_Bit_Register_q2), .Q1(_4_Bit_Register_q1), .Q0(_4_Bit_Register_q0),
    .R(R), .S(S), .CLK(_2xDeMux_a3), .E3(E3), .E2(E2), .E1(E1), .E0(E0));
  _4Bit_Switch_E1E2__A _4Bit_Switch (
    .E1_0(_4_Bit_Register_q3), .E1_1(_4_Bit_Register_q2), .E1_2(_4_Bit_Register_q1),
    .E1_3(_4_Bit_Register_q0), .E2_0(_4_Bit_Register_2_q3), .E2_1(_4_Bit_Register_2_q2),
    .E2_2(_4_Bit_Register_2_q1), .E2_3(_4_Bit_Register_2_q0), .S(A1), .A0(_4Bit_Switch_a0),
    .A1(_4Bit_Switch_a1), .A2(_4Bit_Switch_a2), .A3(_4Bit_Switch_a3));
  _2xDeMux _2xDeMux (.E(W), .S0(A1), .S1(A0), .A3(_2xDeMux_a3), .A2(_2xDeMux_a2), .A1(_2xDeMux_a1), .A0(_2xDeMux_a0));
  _4_Bit_Register__JK _4_Bit_Register_2 (
    .Q3(_4_Bit_Register_2_q3), .Q2(_4_Bit_Register_2_q2), .Q1(_4_Bit_Register_2_q1),
    .Q0(_4_Bit_Register_2_q0), .R(R), .S(S), .CLK(_2xDeMux_a1), .E3(E3), .E2(E2), .E1(E1), .E0(E0));
  _4Bit_Switch_E1E2__A _4Bit_Switch_2 (
    .E1_0(_4Bit_Switch_a0), .E1_1(_4Bit_Switch_a1), .E1_2(_4Bit_Switch_a2), .E1_3(_4Bit_Switch_a3),
    .E2_0(_4Bit_Switch_3_a0), .E2_1(_4Bit_Switch_3_a1), .E2_2(_4Bit_Switch_3_a2), .E2_3(_4Bit_Switch_3_a3),
    .S(A0), .A0(O3), .A1(O2), .A2(O1), .A3(O0));
  _4_Bit_Register__JK _4_Bit_Register_3 (
    .Q3(_4_Bit_Register_3_q3), .Q2(_4_Bit_Register_3_q2), .Q1(_4_Bit_Register_3_q1),
    .Q0(_4_Bit_Register_3_q0), .R(R), .S(S), .CLK(_2xDeMux_a2), .E3(E3), .E2(E2), .E1(E1), .E0(E0));
  _4Bit_Switch_E1E2__A _4Bit_Switch_3 (
    .E1_0(_4_Bit_Register_3_q3), .E1_1(_4_Bit_Register_3_q2), .E1_2(_4_Bit_Register_3_q1),
    .E1_3(_4_Bit_Register_3_q0), .E2_0(_4_Bit_Register_4_q3), .E2_1(_4_Bit_Register_4_q2),
    .E2_2(_4_Bit_Register_4_q1), .E2_3(_4_Bit_Register_4_q0), .S(A1), .A0(_4Bit_Switch_3_a0),
    .A1(_4Bit_Switch_3_a1), .A2(_4Bit_Switch_3_a2), .A3(_4Bit_Switch_3_a3));
  _4_Bit_Register__JK _4_Bit_Register_4 (
    .Q3(_4_Bit_Register_4_q3), .Q2(_4_Bit_Register_4_q2), .Q1(_4_Bit_Register_4_q1),
    .Q0(_4_Bit_Register_4_q0), .R(R), .S(S), .CLK(_2xDeMux_a0), .E3(E3), .E2(E2), .E1(E1), .E0(E0));
endmodule

module _16x4Bit_Ram (
  input  E0,
  input  E1,
  input  E2,
  input  E3,
  input  R,
  input  S,
  input  A0,
  input  A1,
  input  A2,
  input  A3,
  input  W,
  output O3,
  output O3_2,
  output O2,
  output O0
);

  wire _2xDeMux_a0, _2xDeMux_a1, _2xDeMux_a2, _2xDeMux_a3, _4Bit_Switch_3_a0, _4Bit_Switch_3_a1,
       _4Bit_Switch_3_a2, _4Bit_Switch_3_a3, _4Bit_Switch_a0, _4Bit_Switch_a1, _4Bit_Switch_a2,
       _4Bit_Switch_a3, _4x4Bit_Ram_2_o0, _4x4Bit_Ram_2_o1, _4x4Bit_Ram_2_o2, _4x4Bit_Ram_2_o3,
       _4x4Bit_Ram_3_o0, _4x4Bit_Ram_3_o1, _4x4Bit_Ram_3_o2, _4x4Bit_Ram_3_o3, _4x4Bit_Ram_4_o0,
       _4x4Bit_Ram_4_o1, _4x4Bit_Ram_4_o2, _4x4Bit_Ram_4_o3, _4x4Bit_Ram_o0, _4x4Bit_Ram_o1, _4x4Bit_Ram_o2,
       _4x4Bit_Ram_o3;

  _2xDeMux _2xDeMux (.E(W), .S0(A2), .S1(A3), .A3(_2xDeMux_a3), .A2(_2xDeMux_a2), .A1(_2xDeMux_a1), .A0(_2xDeMux_a0));
  _4x4Bit_RAM _4x4Bit_Ram (
    .R(R), .S(S), .E0(E0), .E1(E1), .E2(E2), .E3(E3), .W(_2xDeMux_a3), .A1(A1), .A0(A0), .O3(_4x4Bit_Ram_o3),
    .O2(_4x4Bit_Ram_o2), .O1(_4x4Bit_Ram_o1), .O0(_4x4Bit_Ram_o0));
  _4Bit_Switch_E1E2__A _4Bit_Switch (
    .E1_0(_4x4Bit_Ram_o3), .E1_1(_4x4Bit_Ram_o2), .E1_2(_4x4Bit_Ram_o1), .E1_3(_4x4Bit_Ram_o0),
    .E2_0(_4x4Bit_Ram_2_o3), .E2_1(_4x4Bit_Ram_2_o2), .E2_2(_4x4Bit_Ram_2_o1), .E2_3(_4x4Bit_Ram_2_o0),
    .S(A3), .A0(_4Bit_Switch_a0), .A1(_4Bit_Switch_a1), .A2(_4Bit_Switch_a2), .A3(_4Bit_Switch_a3));
  _4x4Bit_RAM _4x4Bit_Ram_2 (
    .R(R), .S(S), .E0(E0), .E1(E1), .E2(E2), .E3(E3), .W(_2xDeMux_a2), .A1(A1), .A0(A0),
    .O3(_4x4Bit_Ram_2_o3), .O2(_4x4Bit_Ram_2_o2), .O1(_4x4Bit_Ram_2_o1), .O0(_4x4Bit_Ram_2_o0));
  _4Bit_Switch_E1E2__A _4Bit_Switch_2 (
    .E1_0(_4Bit_Switch_a0), .E1_1(_4Bit_Switch_a1), .E1_2(_4Bit_Switch_a2), .E1_3(_4Bit_Switch_a3),
    .E2_0(_4Bit_Switch_3_a0), .E2_1(_4Bit_Switch_3_a1), .E2_2(_4Bit_Switch_3_a2), .E2_3(_4Bit_Switch_3_a3),
    .S(A2), .A0(O3), .A1(O3_2), .A2(O2), .A3(O0));
  _4x4Bit_RAM _4x4Bit_Ram_3 (
    .R(R), .S(S), .E0(E0), .E1(E1), .E2(E2), .E3(E3), .W(_2xDeMux_a1), .A1(A1), .A0(A0),
    .O3(_4x4Bit_Ram_3_o3), .O2(_4x4Bit_Ram_3_o2), .O1(_4x4Bit_Ram_3_o1), .O0(_4x4Bit_Ram_3_o0));
  _4Bit_Switch_E1E2__A _4Bit_Switch_3 (
    .E1_0(_4x4Bit_Ram_3_o3), .E1_1(_4x4Bit_Ram_3_o2), .E1_2(_4x4Bit_Ram_3_o1), .E1_3(_4x4Bit_Ram_3_o0),
    .E2_0(_4x4Bit_Ram_4_o3), .E2_1(_4x4Bit_Ram_4_o2), .E2_2(_4x4Bit_Ram_4_o1), .E2_3(_4x4Bit_Ram_4_o0),
    .S(A3), .A0(_4Bit_Switch_3_a0), .A1(_4Bit_Switch_3_a1), .A2(_4Bit_Switch_3_a2), .A3(_4Bit_Switch_3_a3));
  _4x4Bit_RAM _4x4Bit_Ram_4 (
    .R(R), .S(S), .E0(E0), .E1(E1), .E2(E2), .E3(E3), .W(_2xDeMux_a0), .A1(A1), .A0(A0),
    .O3(_4x4Bit_Ram_4_o3), .O2(_4x4Bit_Ram_4_o2), .O1(_4x4Bit_Ram_4_o1), .O0(_4x4Bit_Ram_4_o0));
endmodule
