// Logisim project Logisim-CPU.circ as structural Verilog
module main (
);
endmodule

module J_K_FlipFlop__logisim (
  input  J,
  input  CLK,
  input  K,
  input  S,
  input  Enable,
  input  R,
  output Q
);

  J_K_Flip_Flop j_k_ff_1 (.J(J), .clk(CLK), .K(K), .Q(Q), .preset(S), .en(Enable), .reset(R));  // open: Qn

  // Notes on the sheet:
  //   J-K Flip Flop
endmodule

module Register_8Bit (
  input  Enable,
  input  CLK,
  input  E1,
  input  E2,
  input  E3,
  input  E4,
  input  E5,
  input  E6,
  input  E7,
  input  E8,
  output A1,
  output A2,
  output A3,
  output A4,
  output A5,
  output A6,
  output A7,
  output A8
);

  D_FlipFlop_mit_Enable D_FlipFlop (.D(E1), .CLK(CLK), .Enable(Enable), .Q(A1));
  D_FlipFlop_mit_Enable D_FlipFlop_2 (.D(E5), .CLK(CLK), .Enable(Enable), .Q(A5));
  D_FlipFlop_mit_Enable D_FlipFlop_3 (.D(E2), .CLK(CLK), .Enable(Enable), .Q(A2));
  D_FlipFlop_mit_Enable D_FlipFlop_4 (.D(E6), .CLK(CLK), .Enable(Enable), .Q(A6));
  D_FlipFlop_mit_Enable D_FlipFlop_5 (.D(E3), .CLK(CLK), .Enable(Enable), .Q(A3));
  D_FlipFlop_mit_Enable D_FlipFlop_6 (.D(E7), .CLK(CLK), .Enable(Enable), .Q(A7));
  D_FlipFlop_mit_Enable D_FlipFlop_7 (.D(E4), .CLK(CLK), .Enable(Enable), .Q(A4));
  D_FlipFlop_mit_Enable D_FlipFlop_8 (.D(E8), .CLK(CLK), .Enable(Enable), .Q(A8));
endmodule

module Register_8Bit__logisim (
  input  E1,
  input  E2,
  input  Enable,
  input  E3,
  input  E4,
  input  CLK,
  input  E5,
  input  E6,
  input  E7,
  input  E8,
  output A1,
  output A2,
  output A3,
  output A4,
  output A5,
  output A6,
  output A7,
  output A8
);

  Register Register_8Bit (
    .D({E8, E7, E6, E5, E4, E3, E2, E1}), .en(Enable), .Q({A8, A7, A6, A5, A4, A3, A2, A1}), .clk(CLK));  // open: clr
endmodule

module J_K_FlipFlop (
  input  S,
  input  J,
  input  CLK,
  input  Enable,
  input  K,
  input  R,
  input  in_7,
  input  in_8,
  input  in_9,
  output A,
  output out_11
);

  wire AND_2_out, AND_3_out, AND_out, NAND_2_out, NAND_3_out, NAND_4_out, NAND_5_out, NAND_6_out, NAND_8_out,
       NAND_out, NOT_2_out, NOT_3_out, NOT_4_out, NOT_out;

  and AND (AND_out, CLK, Enable);
  not NOT (NOT_out, AND_out);
  and AND_2 (AND_2_out, in_7, in_8);
  not NOT_2 (NOT_2_out, S);
  nand NAND (NAND_out, NAND_8_out, J, NOT_out);
  nand NAND_2 (NAND_2_out, NOT_out, K, A);
  not NOT_3 (NOT_3_out, NOT_out);
  not NOT_4 (NOT_4_out, R);
  and AND_3 (AND_3_out, AND_2_out, in_9);
  not NOT_5 (out_11, AND_3_out);
  nand NAND_3 (NAND_3_out, NOT_2_out, NAND_out, NAND_4_out);
  nand NAND_4 (NAND_4_out, NAND_3_out, NAND_2_out, NOT_4_out);
  nand NAND_5 (NAND_5_out, NAND_3_out, NOT_3_out);
  nand NAND_6 (NAND_6_out, NOT_3_out, NAND_4_out);
  nand NAND_7 (A, NOT_2_out, NAND_5_out, NAND_8_out);
  nand NAND_8 (NAND_8_out, A, NAND_6_out, NOT_4_out);

  // Notes on the sheet:
  //   NAND (3 Eingänge)
endmodule

module HalbAddierer (
  input  E1,
  input  E2,
  output A,
  output U
);

  wire AND_2_out, AND_out, NOT_2_out, NOT_out;

  not NOT (NOT_out, E1);
  not NOT_2 (NOT_2_out, E2);
  and AND (AND_out, NOT_out, E2);
  and AND_2 (AND_2_out, NOT_2_out, E1);
  or OR (A, AND_out, AND_2_out);
  and AND_3 (U, E2, E1);
endmodule

module Volladdierer (
  input  E1,
  input  E2,
  input  Ue,
  output A,
  output Ua
);

  wire Halbaddierer_2_u, Halbaddierer_a, Halbaddierer_u;

  HalbAddierer Halbaddierer (.E1(E1), .E2(E2), .A(Halbaddierer_a), .U(Halbaddierer_u));
  HalbAddierer Halbaddierer_2 (.E1(Halbaddierer_a), .E2(Ue), .A(A), .U(Halbaddierer_2_u));
  or OR (Ua, Halbaddierer_2_u, Halbaddierer_u);
endmodule

module Addierer16Bit (
  input  Ue,
  input  X1,
  input  Y1,
  input  X2,
  input  Y2,
  input  X3,
  input  Y3,
  input  X4,
  input  Y4,
  input  X5,
  input  Y5,
  input  X6,
  input  Y6,
  input  X7,
  input  Y7,
  input  X8,
  input  Y8,
  output A1,
  output A2,
  output A3,
  output A4,
  output Ua,
  output A5,
  output A6,
  output A7,
  output A8
);

  wire Volladdierer_2_ua, Volladdierer_3_ua, Volladdierer_4_ua, Volladdierer_5_ua, Volladdierer_6_ua,
       Volladdierer_7_ua, Volladdierer_ua;

  Volladdierer Volladdierer (.E1(Y1), .E2(X1), .Ue(Ue), .A(A1), .Ua(Volladdierer_ua));
  Volladdierer Volladdierer_2 (.E1(Y5), .E2(X5), .Ue(Volladdierer_7_ua), .A(A5), .Ua(Volladdierer_2_ua));
  Volladdierer Volladdierer_3 (.E1(Y2), .E2(X2), .Ue(Volladdierer_ua), .A(A2), .Ua(Volladdierer_3_ua));
  Volladdierer Volladdierer_4 (.E1(Y6), .E2(X6), .Ue(Volladdierer_2_ua), .A(A6), .Ua(Volladdierer_4_ua));
  Volladdierer Volladdierer_5 (.E1(Y3), .E2(X3), .Ue(Volladdierer_3_ua), .A(A3), .Ua(Volladdierer_5_ua));
  Volladdierer Volladdierer_6 (.E1(Y7), .E2(X7), .Ue(Volladdierer_4_ua), .A(A7), .Ua(Volladdierer_6_ua));
  Volladdierer Volladdierer_7 (.E1(Y4), .E2(X4), .Ue(Volladdierer_5_ua), .A(A4), .Ua(Volladdierer_7_ua));
  Volladdierer Volladdierer_8 (.E1(Y8), .E2(X8), .Ue(Volladdierer_6_ua), .A(A8), .Ua(Ua));
endmodule

module Addierer8Bit_logisim (
  input  Ue,
  input  [7:0] X_1_8,
  input  [7:0] Y_1_8,
  output [7:0] A_1_8,
  output Ua
);

  Adder adder_1 (.a(X_1_8), .b(Y_1_8), .out(A_1_8), .cin(Ue), .cout(Ua));
endmodule

module ProgramCounter (
  input  PC_select,
  input  PC_load,
  input  Takt,
  input  [7:0] PC_in,
  output [7:0] PC_out
);

  wire [7:0] adder_1_out, multiplexer_1_out;

  Adder adder_1 (.a(PC_out), .b(8'h1), .out(adder_1_out), .cin(1'b0));  // open: cout
  Multiplexer #(.width(8), .enable("false")) multiplexer_1 (
    .in0(adder_1_out), .in1(PC_in), .out(multiplexer_1_out), .sel(PC_select));
  Register register_1 (.D(multiplexer_1_out), .en(PC_load), .Q(PC_out), .clk(Takt));  // open: clr

  // Notes on the sheet:
  //   Addierer
  //   Multiplexer
  //   Register
endmodule

module ALU_8Bit (
  input  [7:0] X,
  input  [7:0] Y,
  input  [1:0] OP_Select,
  output [7:0] A
);

  wire [7:0] adder_1_out, AND_8Bit_out, multiplexer_1_out, multiplexer_2_out, OR_8Bit_out, subtractor_1_out;

  assign AND_8Bit_out = X & Y;  // AND_Gate AND_8Bit, 8 bits wide
  assign OR_8Bit_out = X | Y;  // OR_Gate OR_8Bit, 8 bits wide
  Adder adder_1 (.a(X), .b(Y), .out(adder_1_out), .cin(1'b0));  // open: cout
  Subtractor subtractor_1 (.a(X), .b(Y), .out(subtractor_1_out), .bin(1'b0));  // open: bout
  Multiplexer #(.width(8), .enable("false")) multiplexer_1 (
    .in0(AND_8Bit_out), .in1(OR_8Bit_out), .out(multiplexer_1_out), .sel(OP_Select[1]));
  Multiplexer #(.width(8), .enable("false")) multiplexer_2 (
    .in0(adder_1_out), .in1(subtractor_1_out), .out(multiplexer_2_out), .sel(OP_Select[1]));
  Multiplexer #(.width(8), .enable("false")) multiplexer_3 (
    .in0(multiplexer_1_out), .in1(multiplexer_2_out), .out(A), .sel(OP_Select[0]));

  // Notes on the sheet:
  //   ADD 8Bit
  //   SUB 8Bit
endmodule

module AND_8Bit (
  input  [7:0] X,
  input  [7:0] Y,
  output [7:0] A
);

  and AND (A[0], X[0], Y[0]);
  and AND_2 (A[1], X[1], Y[1]);
  and AND_3 (A[2], X[2], Y[2]);
  and AND_4 (A[3], X[3], Y[3]);
  and AND_5 (A[4], X[4], Y[4]);
  and AND_6 (A[5], X[5], Y[5]);
  and AND_7 (A[6], X[6], Y[6]);
  and AND_8 (A[7], X[7], Y[7]);
endmodule

module OR_8Bit (
  input  [7:0] X,
  input  [7:0] B,
  output [7:0] A
);

  or OR (A[0], X[0], B[0]);
  or OR_2 (A[1], X[1], B[1]);
  or OR_3 (A[2], X[2], B[2]);
  or OR_4 (A[3], X[3], B[3]);
  or OR_5 (A[4], X[4], B[4]);
  or OR_6 (A[5], X[5], B[5]);
  or OR_7 (A[6], X[6], B[6]);
  or OR_8 (A[7], X[7], B[7]);
endmodule

module NOT_8Bit (
  input  [7:0] X,
  output [7:0] A
);

  not NOT (A[0], X[0]);
  not NOT_2 (A[1], X[1]);
  not NOT_3 (A[2], X[2]);
  not NOT_4 (A[3], X[3]);
  not NOT_5 (A[4], X[4]);
  not NOT_6 (A[5], X[5]);
  not NOT_7 (A[6], X[6]);
  not NOT_8 (A[7], X[7]);
endmodule

module Subtraktion_8Bit (
  input  [7:0] X,
  input  [7:0] Y,
  output [7:0] A
);

  wire [7:0] NOT_8Bit_out;

  assign NOT_8Bit_out = ~Y;  // NOT_Gate NOT_8Bit, 8 bits wide
  Adder adder_1 (.a(X), .b(NOT_8Bit_out), .out(A), .cin(1'b1));  // open: cout

  // Notes on the sheet:
  //   Ue
  //   Addierer
endmodule

module RegisterR1R2R3R4 (
  input  Write,
  input  [1:0] DestinationRegSelect,
  input  [7:0] DataIn,
  input  Takt,
  input  [1:0] SourceRegisterSelect,
  output [7:0] DestiantionBusOut,
  output ZeroFlag,
  output NegativFlag,
  output [7:0] SourceBusOut,
  output [7:0] R1,
  output [7:0] R2,
  output [7:0] R3,
  output [7:0] R4
);

  wire demultiplexer_1_out0, demultiplexer_1_out1, demultiplexer_1_out2, demultiplexer_1_out3, OR_8x_out;

  Demultiplexer #(.select(2), .enable("false")) demultiplexer_1 (
    .out0(demultiplexer_1_out0), .out1(demultiplexer_1_out1), .out2(demultiplexer_1_out2),
    .out3(demultiplexer_1_out3), .in(Write), .sel(DestinationRegSelect));
  Register register_1 (.D(DataIn), .en(demultiplexer_1_out0), .Q(R1), .clk(Takt));  // open: clr
  Register register_2 (.D(DataIn), .en(demultiplexer_1_out1), .Q(R2), .clk(Takt));  // open: clr
  Register register_3 (.D(DataIn), .en(demultiplexer_1_out2), .Q(R3), .clk(Takt));  // open: clr
  Register register_4 (.D(DataIn), .en(demultiplexer_1_out3), .Q(R4), .clk(Takt));  // open: clr
  Multiplexer #(.select(2), .width(8), .enable("false")) multiplexer_1 (
    .in0(R1), .in1(R2), .in2(R3), .in3(R4), .out(DestiantionBusOut), .sel(DestinationRegSelect));
  Multiplexer #(.select(2), .width(8), .enable("false")) multiplexer_2 (
    .in0(R1), .in1(R2), .in2(R3), .in3(R4), .out(SourceBusOut), .sel(SourceRegisterSelect));
  or OR_8x (OR_8x_out, DestiantionBusOut[0], DestiantionBusOut[1], DestiantionBusOut[2], DestiantionBusOut[3], DestiantionBusOut[4], DestiantionBusOut[5], DestiantionBusOut[6], DestiantionBusOut[7]);
  not NOT (ZeroFlag, OR_8x_out);

  assign NegativFlag = DestiantionBusOut[7];

  // Notes on the sheet:
  //   Demultiplexer
  //   R1
  //   R2
  //   R3
  //   R4
endmodule

module ALU_Reg (
  input  [7:0] Immediat,
  input  [7:0] DataIn,
  input  [1:0] RegSel,
  input  [1:0] dRegSel,
  input  [1:0] sRegSel,
  input  RegWrite,
  input  Takt,
  input  [1:0] OP_Select,
  output [7:0] sBus,
  output [7:0] DataInRegister,
  output ZeroFlag,
  output NegativFlag,
  output [7:0] dBus,
  output [7:0] AluOut,
  output [7:0] R1,
  output [7:0] R2,
  output [7:0] R3,
  output [7:0] R4
);

  Multiplexer #(.select(2), .width(8), .enable("false")) multiplexer_1 (
    .in0(Immediat), .in1(sBus), .in2(DataIn), .in3(AluOut), .out(DataInRegister), .sel(RegSel));
  RegisterR1R2R3R4 Register (
    .Write(RegWrite), .DestinationRegSelect(dRegSel), .DataIn(DataInRegister),
    .SourceRegisterSelect(sRegSel), .R1(R1), .Takt(Takt), .R2(R2), .R3(R3), .R4(R4),
    .DestiantionBusOut(dBus), .ZeroFlag(ZeroFlag), .NegativFlag(NegativFlag), .SourceBusOut(sBus));
  ALU_8Bit ALU (.X(dBus), .Y(sBus), .OP_Select(OP_Select), .A(AluOut));
endmodule

module Multiplexer_1Bit (
  input  E1,
  input  E2,
  input  S,
  output A
);

  wire AND_2_out, AND_out, NOT_out;

  not NOT (NOT_out, S);
  and AND (AND_out, E1, NOT_out);
  and AND_2 (AND_2_out, E2, S);
  or OR (A, AND_out, AND_2_out);
endmodule

module Multiplexer_8Bit (
  input  [7:0] E1,
  input  [7:0] E2,
  input  S,
  output [7:0] out_4
);

  Multiplexer_1Bit MUX_1Bit_2x (.E1(E1[0]), .E2(E2[0]), .S(S), .A(out_4[0]));
  Multiplexer_1Bit MUX_1Bit_2x_2 (.E1(E1[1]), .E2(E2[1]), .S(S), .A(out_4[1]));
  Multiplexer_1Bit MUX_1Bit_2x_3 (.E1(E1[2]), .E2(E2[2]), .S(S), .A(out_4[2]));
  Multiplexer_1Bit MUX_1Bit_2x_4 (.E1(E1[3]), .E2(E2[3]), .S(S), .A(out_4[3]));
  Multiplexer_1Bit MUX_1Bit_2x_5 (.E1(E1[4]), .E2(E2[4]), .S(S), .A(out_4[4]));
  Multiplexer_1Bit MUX_1Bit_2x_6 (.E1(E1[5]), .E2(E2[5]), .S(S), .A(out_4[5]));
  Multiplexer_1Bit MUX_1Bit_2x_7 (.E1(E1[6]), .E2(E2[6]), .S(S), .A(out_4[6]));
  Multiplexer_1Bit MUX_1Bit_2x_8 (.E1(E1[7]), .E2(S), .S(E2[7]), .A(out_4[7]));
endmodule

module DeMultiplexer_1Bit (
  input  E,
  input  S,
  output A1,
  output A2
);

  wire NOT_out;

  not NOT (NOT_out, S);
  and AND (A1, NOT_out, E);
  and AND_2 (A2, E, S);
endmodule

module DeMultiplexer_8Bit (
  input  [7:0] E,
  input  S,
  output [7:0] A1,
  output [7:0] A2
);

  DeMultiplexer_1Bit DeMUX_1Bit_2x (.E(E[0]), .S(S), .A1(A1[0]), .A2(A2[0]));
  DeMultiplexer_1Bit DeMUX_1Bit_2 (.E(E[1]), .S(S), .A1(A1[1]), .A2(A2[1]));
  DeMultiplexer_1Bit DeMUX_1Bit_2x_2 (.E(E[2]), .S(S), .A1(A1[2]), .A2(A2[2]));
  DeMultiplexer_1Bit DeMUX_1Bit_2x_3 (.E(E[3]), .S(S), .A1(A1[3]), .A2(A2[3]));
  DeMultiplexer_1Bit DeMUX_1Bit_2x_4 (.E(E[4]), .S(S), .A1(A1[4]), .A2(A2[4]));
  DeMultiplexer_1Bit DeMUX_1Bit_2x_5 (.E(E[5]), .S(S), .A1(A1[5]), .A2(A2[5]));
  DeMultiplexer_1Bit DeMUX_1Bit_2x_6 (.E(E[6]), .S(S), .A1(A1[6]), .A2(A2[6]));
  DeMultiplexer_1Bit DeMUX_1Bit_2x_7 (.E(E[7]), .S(S), .A1(A1[7]), .A2(A2[7]));
endmodule

module Multiplxer_8Bit_4x (
  input  [7:0] E1,
  input  [7:0] E2,
  input  [7:0] E3,
  input  [7:0] E4,
  input  [1:0] S,
  output [7:0] A
);

  wire [7:0] MUX_8Bit_2x_2_out_4, MUX_8Bit_2x_out_4;

  Multiplexer_8Bit MUX_8Bit_2x (.E1(E1), .E2(E2), .S(S[0]), .out_4(MUX_8Bit_2x_out_4));
  Multiplexer_8Bit MUX_8Bit_2x_2 (.E1(E3), .E2(E4), .S(S[0]), .out_4(MUX_8Bit_2x_2_out_4));
  Multiplexer_8Bit MUX_8Bit_2x_3 (.E1(MUX_8Bit_2x_out_4), .E2(MUX_8Bit_2x_2_out_4), .S(S[1]), .out_4(A));
endmodule

module DeMultiplexer_8Bit_4x (
  input  [7:0] E,
  input  [1:0] S,
  output [7:0] A1,
  output [7:0] A2,
  output [7:0] A3,
  output [7:0] A4
);

  wire [7:0] DeMux_8Bit_2x_a1, DeMux_8Bit_2x_a2;

  DeMultiplexer_8Bit DeMux_8Bit_2x (.E(E), .S(S[1]), .A1(DeMux_8Bit_2x_a1), .A2(DeMux_8Bit_2x_a2));
  DeMultiplexer_8Bit DeMux_8Bit_2x_2 (.E(DeMux_8Bit_2x_a1), .S(S[0]), .A1(A1), .A2(A2));
  DeMultiplexer_8Bit DeMux_8Bit_2x_3 (.E(DeMux_8Bit_2x_a2), .S(S[0]), .A1(A3), .A2(A4));
endmodule

module DeMultiplexer_1Bit_2x (
  input  E,
  input  [1:0] S,
  output A1,
  output A2,
  output A3,
  output A4
);

  wire DeMUX_1Bit_2x_a1, DeMUX_1Bit_2x_a2;

  DeMultiplexer_1Bit DeMUX_1Bit_2x (.E(E), .S(S[1]), .A1(DeMUX_1Bit_2x_a1), .A2(DeMUX_1Bit_2x_a2));
  DeMultiplexer_1Bit DeMUX_1Bit_2x_2 (.E(DeMUX_1Bit_2x_a1), .S(S[0]), .A1(A1), .A2(A2));
  DeMultiplexer_1Bit DeMUX_1Bit_2x_3 (.E(DeMUX_1Bit_2x_a2), .S(S[0]), .A1(A3), .A2(A4));
endmodule

module DeMultiplexer_1Bit_16x (
  input  A,
  input  [3:0] S,
  output A1,
  output A2,
  output A3,
  output A4,
  output A5,
  output A6,
  output A7,
  output A8,
  output A9,
  output A10,
  output A11,
  output A12,
  output A13,
  output A14,
  output A15,
  output A16
);

  wire DeMUX_1Bit_2x_a1, DeMUX_1Bit_2x_a2, DeMUX_1Bit_2x_a3, DeMUX_1Bit_2x_a4;

  DeMultiplexer_1Bit_2x DeMUX_1Bit_2x (
    .E(A), .S(S[3:2]), .A1(DeMUX_1Bit_2x_a1), .A2(DeMUX_1Bit_2x_a2), .A3(DeMUX_1Bit_2x_a3),
    .A4(DeMUX_1Bit_2x_a4));
  DeMultiplexer_1Bit_2x DeMUX_1Bit_2x_2 (.E(DeMUX_1Bit_2x_a1), .S(S[1:0]), .A1(A1), .A2(A2), .A3(A3), .A4(A4));
  DeMultiplexer_1Bit_2x DeMUX_1Bit_2x_3 (.E(DeMUX_1Bit_2x_a2), .S(S[1:0]), .A1(A5), .A2(A6), .A3(A7), .A4(A8));
  DeMultiplexer_1Bit_2x DeMUX_1Bit_2x_4 (.E(DeMUX_1Bit_2x_a3), .S(S[1:0]), .A1(A9), .A2(A10), .A3(A11), .A4(A12));
  DeMultiplexer_1Bit_2x DeMUX_1Bit_2x_5 (.E(DeMUX_1Bit_2x_a4), .S(S[1:0]), .A1(A13), .A2(A14), .A3(A15), .A4(A16));
endmodule

module Multiplex_8Bit_16x (
  input  [7:0] E1,
  input  [7:0] E2,
  input  [7:0] E3,
  input  [7:0] E4,
  input  [7:0] E5,
  input  [7:0] E6,
  input  [7:0] E7,
  input  [7:0] E8,
  input  [7:0] E9,
  input  [7:0] E10,
  input  [7:0] E11,
  input  [7:0] E12,
  input  [7:0] E13,
  input  [7:0] E14,
  input  [7:0] E15,
  input  [7:0] E16,
  input  [3:0] S,
  output [7:0] A
);

  wire [7:0] MUX_8Bit_4x_2_a, MUX_8Bit_4x_3_a, MUX_8Bit_4x_4_a, MUX_8Bit_4x_a;

  Multiplxer_8Bit_4x MUX_8Bit_4x (.E1(E1), .E2(E2), .E3(E3), .E4(E4), .S(S[1:0]), .A(MUX_8Bit_4x_a));
  Multiplxer_8Bit_4x MUX_8Bit_4x_2 (.E1(E5), .E2(E6), .E3(E7), .E4(E8), .S(S[1:0]), .A(MUX_8Bit_4x_2_a));
  Multiplxer_8Bit_4x MUX_8Bit_4x_3 (.E1(E9), .E2(E10), .E3(E11), .E4(E12), .S(S[1:0]), .A(MUX_8Bit_4x_3_a));
  Multiplxer_8Bit_4x MUX_8Bit_4x_4 (.E1(E13), .E2(E14), .E3(E15), .E4(E16), .S(S[1:0]), .A(MUX_8Bit_4x_4_a));
  Multiplxer_8Bit_4x MUX_8Bit_4x_5 (
    .E1(MUX_8Bit_4x_a), .E2(MUX_8Bit_4x_2_a), .E3(MUX_8Bit_4x_3_a), .E4(MUX_8Bit_4x_4_a), .S(S[3:2]), .A(A));
endmodule

module RAM_A8BitD8Bit (
  input  Takt,
  input  Write,
  input  [7:0] Adresse,
  input  [7:0] DataIn,
  output [7:0] DataOut
);

  wire demultiplexer_1bit_16x_1_a1, demultiplexer_1bit_16x_1_a2, demultiplexer_1bit_16x_1_a3,
       demultiplexer_1bit_16x_1_a4, demultiplexer_1bit_16x_1_a5, demultiplexer_1bit_16x_1_a6,
       demultiplexer_1bit_16x_1_a7, demultiplexer_1bit_16x_1_a8, demultiplexer_1bit_16x_1_a9,
       demultiplexer_1bit_16x_1_a10, demultiplexer_1bit_16x_1_a11, demultiplexer_1bit_16x_1_a12,
       demultiplexer_1bit_16x_1_a13, demultiplexer_1bit_16x_1_a14, demultiplexer_1bit_16x_1_a15,
       demultiplexer_1bit_16x_1_a16;
  wire [7:0] Register_8Bit_2_q, Register_8Bit_3_q, Register_8Bit_4_q, Register_8Bit_5_q, Register_8Bit_6_q,
       Register_8Bit_7_q, Register_8Bit_8_q, Register_8Bit_9_q, Register_8Bit_10_q, Register_8Bit_11_q,
       Register_8Bit_12_q, Register_8Bit_13_q, Register_8Bit_14_q, Register_8Bit_15_q, Register_8Bit_16_q,
       Register_8Bit_q;

  DeMultiplexer_1Bit_16x demultiplexer_1bit_16x_1 (
    .A(Write), .S(Adresse[3:0]), .A1(demultiplexer_1bit_16x_1_a1), .A2(demultiplexer_1bit_16x_1_a2),
    .A3(demultiplexer_1bit_16x_1_a3), .A4(demultiplexer_1bit_16x_1_a4), .A5(demultiplexer_1bit_16x_1_a5),
    .A6(demultiplexer_1bit_16x_1_a6), .A7(demultiplexer_1bit_16x_1_a7), .A8(demultiplexer_1bit_16x_1_a8),
    .A9(demultiplexer_1bit_16x_1_a9), .A10(demultiplexer_1bit_16x_1_a10), .A11(demultiplexer_1bit_16x_1_a11),
    .A12(demultiplexer_1bit_16x_1_a12), .A13(demultiplexer_1bit_16x_1_a13),
    .A14(demultiplexer_1bit_16x_1_a14), .A15(demultiplexer_1bit_16x_1_a15), .A16(demultiplexer_1bit_16x_1_a16));
  Register Register_8Bit (.D(DataIn), .en(demultiplexer_1bit_16x_1_a1), .Q(Register_8Bit_q), .clk(Takt));  // open: clr
  Register Register_8Bit_2 (
    .D(DataIn), .en(demultiplexer_1bit_16x_1_a2), .Q(Register_8Bit_2_q), .clk(Takt));  // open: clr
  Register Register_8Bit_3 (
    .D(DataIn), .en(demultiplexer_1bit_16x_1_a3), .Q(Register_8Bit_3_q), .clk(Takt));  // open: clr
  Register Register_8Bit_4 (
    .D(DataIn), .en(demultiplexer_1bit_16x_1_a4), .Q(Register_8Bit_4_q), .clk(Takt));  // open: clr
  Register Register_8Bit_5 (
    .D(DataIn), .en(demultiplexer_1bit_16x_1_a5), .Q(Register_8Bit_5_q), .clk(Takt));  // open: clr
  Register Register_8Bit_6 (
    .D(DataIn), .en(demultiplexer_1bit_16x_1_a6), .Q(Register_8Bit_6_q), .clk(Takt));  // open: clr
  Register Register_8Bit_7 (
    .D(DataIn), .en(demultiplexer_1bit_16x_1_a7), .Q(Register_8Bit_7_q), .clk(Takt));  // open: clr
  Register Register_8Bit_8 (
    .D(DataIn), .en(demultiplexer_1bit_16x_1_a8), .Q(Register_8Bit_8_q), .clk(Takt));  // open: clr
  Register Register_8Bit_9 (
    .D(DataIn), .en(demultiplexer_1bit_16x_1_a9), .Q(Register_8Bit_9_q), .clk(Takt));  // open: clr
  Register Register_8Bit_10 (
    .D(DataIn), .en(demultiplexer_1bit_16x_1_a10), .Q(Register_8Bit_10_q), .clk(Takt));  // open: clr
  Register Register_8Bit_11 (
    .D(DataIn), .en(demultiplexer_1bit_16x_1_a11), .Q(Register_8Bit_11_q), .clk(Takt));  // open: clr
  Register Register_8Bit_12 (
    .D(DataIn), .en(demultiplexer_1bit_16x_1_a12), .Q(Register_8Bit_12_q), .clk(Takt));  // open: clr
  Register Register_8Bit_13 (
    .D(DataIn), .en(demultiplexer_1bit_16x_1_a13), .Q(Register_8Bit_13_q), .clk(Takt));  // open: clr
  Register Register_8Bit_14 (
    .D(DataIn), .en(demultiplexer_1bit_16x_1_a14), .Q(Register_8Bit_14_q), .clk(Takt));  // open: clr
  Register Register_8Bit_15 (
    .D(DataIn), .en(demultiplexer_1bit_16x_1_a15), .Q(Register_8Bit_15_q), .clk(Takt));  // open: clr
  Register Register_8Bit_16 (
    .D(DataIn), .en(demultiplexer_1bit_16x_1_a16), .Q(Register_8Bit_16_q), .clk(Takt));  // open: clr
  Multiplex_8Bit_16x MUX_8Bit_16x (
    .E1(Register_8Bit_q), .E2(Register_8Bit_2_q), .E3(Register_8Bit_3_q), .E4(Register_8Bit_4_q),
    .E5(Register_8Bit_5_q), .E6(Register_8Bit_6_q), .E7(Register_8Bit_7_q), .E8(Register_8Bit_8_q),
    .E9(Register_8Bit_9_q), .E10(Register_8Bit_10_q), .E11(Register_8Bit_11_q), .E12(Register_8Bit_12_q),
    .E13(Register_8Bit_13_q), .E14(Register_8Bit_14_q), .E15(Register_8Bit_15_q), .E16(Register_8Bit_16_q),
    .S(Adresse[3:0]), .A(DataOut));

  // Notes on the sheet:
  //   DeMUX 1Bit 16x
endmodule

module RAM_AdressBus (
  input  [7:0] sourceBus,
  input  [7:0] destinationBus,
  input  PCSelect,
  input  [1:0] AdressSelect,
  input  PCLoad,
  input  [7:0] DataInBus,
  input  Takt,
  input  Write,
  input  InstructionLoad,
  input  ImmediateLoad,
  output [7:0] AdressBus,
  output [7:0] DataOutBus,
  output [7:0] Instruction,
  output [7:0] Immediate
);

  wire [7:0] PC_Counter_8Bit_pc_out;

  ProgramCounter PC_Counter_8Bit (
    .PC_in(Immediate), .PC_select(PCSelect), .PC_load(PCLoad), .Takt(Takt), .PC_out(PC_Counter_8Bit_pc_out));
  Multiplexer #(.select(2), .width(8), .enable("false")) multiplexer_1 (
    .in0(PC_Counter_8Bit_pc_out), .in1(Immediate), .in2(sourceBus), .in3(destinationBus), .out(AdressBus),
    .sel(AdressSelect));
  RAM #(.bus("separate")) ram_1 (
    .addr(AdressBus), .din(DataInBus), .data(DataOutBus), .str(Write), .clk(Takt));  // open: sel, ld, clr
  Register Register_8Bit_InstReg (.D(DataOutBus), .en(InstructionLoad), .Q(Instruction), .clk(Takt));  // open: clr
  Register Register_8Bit_ImmedReg (.D(DataOutBus), .en(ImmediateLoad), .Q(Immediate), .clk(Takt));  // open: clr

  // Notes on the sheet:
  //   MUX 8Bit 4x
  //   RAM 256Byte 8Bit Daten 8Bit Adress
endmodule

module RAM_ALU (
  input  PCSel,
  input  [1:0] AddressSel,
  input  PCLoad,
  input  Takt,
  input  Write,
  input  InstructionLoad,
  input  ImmediateLoad,
  input  RegWrite,
  input  [1:0] RegSel,
  input  [1:0] dRegSel,
  input  [1:0] sRegSel,
  input  [1:0] opSel,
  output [7:0] DataInReg,
  output [7:0] AdressBus,
  output [7:0] DataBus,
  output [7:0] Instruction,
  output [7:0] dBus,
  output [7:0] sBus,
  output [7:0] Immediate,
  output ZeroFlag,
  output NegativFlag,
  output [7:0] ALUout,
  output [7:0] R1,
  output [7:0] R2,
  output [7:0] R3,
  output [7:0] R4
);

  RAM_AdressBus RAM_AB (
    .sourceBus(sBus), .destinationBus(dBus), .PCSelect(PCSel), .AdressSelect(AddressSel), .PCLoad(PCLoad),
    .DataInBus(dBus), .Takt(Takt), .Write(Write), .InstructionLoad(InstructionLoad),
    .ImmediateLoad(ImmediateLoad), .AdressBus(AdressBus), .DataOutBus(DataBus), .Instruction(Instruction),
    .Immediate(Immediate));
  ALU_Reg ALU_Reg (
    .Immediat(Immediate), .DataIn(DataBus), .DataInRegister(DataInReg), .ZeroFlag(ZeroFlag),
    .NegativFlag(NegativFlag), .sBus(sBus), .dBus(dBus), .AluOut(ALUout), .RegSel(RegSel), .dRegSel(dRegSel),
    .sRegSel(sRegSel), .RegWrite(RegWrite), .R1(R1), .Takt(Takt), .R2(R2), .R3(R3), .OP_Select(opSel), .R4(R4));

  // Notes on the sheet:
  //   DataInBus
  //   Immediate ->
  //   DataOut->DataIn
endmodule

module D_FlipFlop_mit_Enable (
  input  D,
  input  CLK,
  input  Enable,
  output Q
);

  wire AND_out, NAND_2_out, NAND_4_out, NAND_out, not_1_out;

  and AND (AND_out, CLK, Enable);
  not not_1 (not_1_out, D);
  nand NAND (NAND_out, D, AND_out);
  nand NAND_2 (NAND_2_out, AND_out, not_1_out);
  nand NAND_3 (Q, NAND_out, NAND_4_out);
  nand NAND_4 (NAND_4_out, Q, NAND_2_out);
endmodule

module D_FlipFlop__Logisim (
  input  CLK,
  input  D,
  input  Enable,
  output Q
);

  D_Flip_Flop D_FlipFlop (.clk(CLK), .D(D), .Q(Q), .en(Enable));  // open: Qn, preset, reset
endmodule

module ZyklusCounter (
  input  Takt,
  output Zyklus_3,
  output Zyklus_2,
  output Zyklus_1,
  output [7:0] Counter
);

  wire NOT_2_out, NOT_3_out, NOT_4_out, NOT_out;
  wire [7:0] adder_1_out, multiplexer_1_out;

  Adder adder_1 (.a(Counter), .b(8'h1), .out(adder_1_out));  // open: cin, cout
  Multiplexer #(.width(8), .enable("false")) multiplexer_1 (
    .in0(adder_1_out), .in1({8{1'b0}}), .out(multiplexer_1_out), .sel(Zyklus_3));
  Register Register_8Bit (.D(multiplexer_1_out), .Q(Counter), .clk(Takt));  // open: en, clr
  not NOT (NOT_out, Counter[0]);
  not NOT_2 (NOT_2_out, Counter[1]);
  not NOT_3 (NOT_3_out, Counter[0]);
  not NOT_4 (NOT_4_out, Counter[1]);
  and AND (Zyklus_3, Counter[1], NOT_out);
  and AND_2 (Zyklus_2, Counter[0], NOT_2_out);
  and AND_3 (Zyklus_1, NOT_3_out, NOT_4_out);

  // Notes on the sheet:
  //   Adder 8Bit
  //   MUX 8Bit 2x
endmodule

module CommandDecoder (
  input  [7:0] InstructionReg,
  input  E1,
  input  E2,
  input  E3,
  output LDR,
  output STR,
  output A,
  output MR1R2,
  output JPZ,
  output AND,
  output OR,
  output ADD,
  output SUB
);

  wire AND_out, not_1_out, not_2_out, not_3_out, not_4_out, not_5_out, not_6_out, not_7_out, not_8_out,
       not_9_out, not_10_out, not_11_out, not_12_out;

  and u_AND (AND_out, E1, E2);
  and AND_2 (A, AND_out, E3);
  not not_1 (not_1_out, InstructionReg[0]);
  not not_2 (not_2_out, InstructionReg[1]);
  not not_3 (not_3_out, InstructionReg[2]);
  not not_4 (not_4_out, InstructionReg[1]);
  not not_5 (not_5_out, InstructionReg[2]);
  not not_6 (not_6_out, InstructionReg[0]);
  not not_7 (not_7_out, InstructionReg[2]);
  not not_8 (not_8_out, InstructionReg[2]);
  not not_9 (not_9_out, InstructionReg[0]);
  not not_10 (not_10_out, InstructionReg[1]);
  not not_11 (not_11_out, InstructionReg[1]);
  not not_12 (not_12_out, InstructionReg[0]);
  and AND_3x (LDR, not_1_out, not_2_out, not_3_out);
  and AND_3x_2 (STR, InstructionReg[0], not_4_out, not_5_out);
  and AND_3x_3 (MR1R2, not_6_out, InstructionReg[1], not_7_out);
  and AND_3x_4 (JPZ, InstructionReg[0], InstructionReg[1], not_8_out);
  and AND_3x_5 (AND, not_9_out, not_10_out, InstructionReg[2]);
  and AND_3x_6 (OR, InstructionReg[0], not_11_out, InstructionReg[2]);
  and AND_3x_7 (ADD, not_12_out, InstructionReg[1], InstructionReg[2]);
  and AND_3x_8 (SUB, InstructionReg[0], InstructionReg[1], InstructionReg[2]);

  // Notes on the sheet:
  //   AND 3x
  //   NOT
endmodule

module OR_1Bit_8x (
  input  E1,
  input  E1_2,
  input  E2,
  input  E3,
  input  E2_2,
  input  E3_2,
  input  E4,
  input  E5,
  input  E4_2,
  input  E5_2,
  input  E6,
  input  E7,
  input  E8,
  input  E1_3,
  input  E1_4,
  input  E2_3,
  input  E2_4,
  input  E3_3,
  input  E3_4,
  input  E4_3,
  output A,
  output A_2,
  output A_3,
  output A_4
);

  wire OR_2_out, OR_3_out, OR_4_out, OR_5_out, OR_6_out, OR_7_out, OR_8_out, OR_11_out, OR_12_out, OR_13_out,
       OR_14_out, OR_out;

  or OR (OR_out, E1, E2);
  or OR_2 (OR_2_out, E3, E4);
  or OR_3 (OR_3_out, E5, E6);
  or OR_4 (OR_4_out, E7, E8);
  or OR_5 (OR_5_out, E1_4, E2_4);
  or OR_6 (OR_6_out, E3_3, E4_3);
  or OR_7 (OR_7_out, OR_out, OR_2_out);
  or OR_8 (OR_8_out, OR_3_out, OR_4_out);
  or OR_9 (A_4, OR_5_out, OR_6_out);
  or OR_10 (A_2, OR_7_out, OR_8_out);
  or OR_11 (OR_11_out, E1_2, E2_2);
  or OR_12 (OR_12_out, E3_2, E4_2);
  or OR_13 (OR_13_out, E1_3, E2_3);
  or OR_14 (OR_14_out, OR_11_out, OR_12_out);
  or OR_15 (A_3, OR_13_out, E3_4);
  or OR_16 (A, OR_14_out, E5_2);

  // Notes on the sheet:
  //   OR 1Bit 8x
  //   OR 1Bit 4x
  //   OR 1Bit 5x
  //   OR 1Bit 3x
endmodule

module CommandSet (
  input  [7:0] Zyklus,
  input  LDR,
  input  STR,
  input  JPZ,
  input  MR1R2,
  input  AND,
  input  OR,
  input  ADD,
  input  SUB,
  input  zFlag,
  output PCSel,
  output PCLoad,
  output Write,
  output InstructionLoad,
  output ImmediateLoad,
  output RegWrite,
  output [1:0] RegSel,
  output [1:0] dRegSel,
  output [1:0] sRegSel,
  output [1:0] opSel,
  output [1:0] AddressSel
);

  wire AND_out, OR_2_out, OR_3_out, OR_3x_out, OR_4_out, OR_4x_out, OR_5_out, OR_5x_out, OR_out;

  or u_OR (OR_out, LDR, STR);
  and u_AND (AND_out, JPZ, zFlag);
  or OR_2 (OR_2_out, OR, SUB);
  or OR_3 (OR_3_out, SUB, ADD);
  or OR_3x (OR_3x_out, LDR, STR, JPZ);
  or OR_4 (OR_4_out, STR, AND_out);
  or OR_5x (OR_5x_out, MR1R2, AND, OR, ADD, SUB);
  or OR_4x (OR_4x_out, AND, OR, ADD, SUB);
  or OR_5 (OR_5_out, OR_4x_out, MR1R2);
  Multiplexer #(.select(2), .enable("false")) multiplexer_1 (
    .in0(1'b0), .in1(1'b0), .in2(JPZ), .in3(1'b0), .out(PCSel), .sel(Zyklus[1:0]));
  Multiplexer #(.select(2), .enable("false")) multiplexer_2 (
    .in0(1'b1), .in1(OR_3x_out), .in2(1'b0), .in3(1'b0), .out(PCLoad), .sel(Zyklus[1:0]));
  Multiplexer #(.select(2), .enable("false")) multiplexer_3 (
    .in0(1'b0), .in1(1'b0), .in2(OR_4_out), .in3(1'b0), .out(Write), .sel(Zyklus[1:0]));
  Multiplexer #(.select(2), .enable("false")) multiplexer_4 (
    .in0(1'b1), .in1(1'b0), .in2(1'b0), .in3(1'b0), .out(InstructionLoad), .sel(Zyklus[1:0]));
  Multiplexer #(.select(2), .enable("false")) multiplexer_5 (
    .in0(1'b0), .in1(OR_3x_out), .in2(1'b0), .in3(1'b0), .out(ImmediateLoad), .sel(Zyklus[1:0]));
  Multiplexer #(.select(2), .enable("false")) multiplexer_6 (
    .in0(1'b0), .in1(OR_5x_out), .in2(LDR), .in3(1'b0), .out(RegWrite), .sel(Zyklus[1:0]));
  Multiplexer #(.select(2), .enable("false")) multiplexer_7 (
    .in0(1'b0), .in1(OR_5_out), .in2(1'b0), .in3(1'b0), .out(RegSel[0]), .sel(Zyklus[1:0]));
  Multiplexer #(.select(2), .enable("false")) multiplexer_8 (
    .in0(1'b0), .in1(OR_4x_out), .in2(LDR), .in3(1'b0), .out(RegSel[1]), .sel(Zyklus[1:0]));
  Multiplexer #(.select(2), .enable("false")) multiplexer_9 (
    .in0(1'b0), .in1(MR1R2), .in2(1'b0), .in3(1'b0), .out(dRegSel[0]), .sel(Zyklus[1:0]));
  Multiplexer #(.select(2), .enable("false")) multiplexer_10 (
    .in0(1'b0), .in1(OR_4x_out), .in2(1'b0), .in3(1'b0), .out(sRegSel[0]), .sel(Zyklus[1:0]));
  Multiplexer #(.select(2), .enable("false")) multiplexer_11 (
    .in0(1'b0), .in1(OR_2_out), .in2(1'b0), .in3(1'b0), .out(opSel[0]), .sel(Zyklus[1:0]));
  Multiplexer #(.select(2), .enable("false")) multiplexer_12 (
    .in0(1'b0), .in1(OR_3_out), .in2(1'b0), .in3(1'b0), .out(opSel[1]), .sel(Zyklus[1:0]));
  Multiplexer #(.select(2), .enable("false")) multiplexer_13 (
    .in0(1'b0), .in1(1'b0), .in2(OR_out), .in3(1'b0), .out(AddressSel[0]), .sel(Zyklus[1:0]));

  assign AddressSel[1] = 1'b0;
  assign dRegSel[1] = 1'b0;
  assign sRegSel[1] = 1'b0;

  // Notes on the sheet:
  //   MUX 1Bit 4x
endmodule

module Multiplexer_1Bit_4x (
  input  E1,
  input  E2,
  input  E3,
  input  E4,
  input  [1:0] S,
  output A
);

  wire MUX_1Bit_4x_2_a, MUX_1Bit_4x_a;

  Multiplexer_1Bit MUX_1Bit_4x (.E1(E1), .E2(E2), .S(S[0]), .A(MUX_1Bit_4x_a));
  Multiplexer_1Bit MUX_1Bit_4x_2 (.E1(E3), .E2(E4), .S(S[0]), .A(MUX_1Bit_4x_2_a));
  Multiplexer_1Bit MUX_1Bit_4x_3 (.E1(MUX_1Bit_4x_a), .E2(MUX_1Bit_4x_2_a), .S(S[1]), .A(A));
endmodule

module CPU_Controller (
  input  [7:0] InstructionReg,
  input  zFlag,
  input  Takt,
  output PCSel,
  output PCLoad,
  output Write,
  output InstructionLoad,
  output ImmediateLoad,
  output RegWrite,
  output [1:0] RegSel,
  output [1:0] dRegSel,
  output [1:0] sRegSel,
  output [1:0] opSel,
  output [1:0] AddressSel,
  output [7:0] Zyklus
);

  wire Command_Dekoder_add, Command_Dekoder_and, Command_Dekoder_jpz, Command_Dekoder_ldr,
       Command_Dekoder_mr1r2, Command_Dekoder_or, Command_Dekoder_str, Command_Dekoder_sub;

  CommandDecoder Command_Dekoder (
    .InstructionReg(InstructionReg), .LDR(Command_Dekoder_ldr), .STR(Command_Dekoder_str),
    .MR1R2(Command_Dekoder_mr1r2), .JPZ(Command_Dekoder_jpz), .AND(Command_Dekoder_and),
    .OR(Command_Dekoder_or), .ADD(Command_Dekoder_add), .SUB(Command_Dekoder_sub));  // open: A, E1, E2, E3
  ZyklusCounter ZyklusCounter (.Takt(Takt), .Counter(Zyklus));  // open: Zyklus_3, Zyklus_2, Zyklus_1
  CommandSet CommandSet (
    .Zyklus(Zyklus), .LDR(Command_Dekoder_ldr), .STR(Command_Dekoder_str), .JPZ(Command_Dekoder_jpz),
    .MR1R2(Command_Dekoder_mr1r2), .AND(Command_Dekoder_and), .OR(Command_Dekoder_or),
    .ADD(Command_Dekoder_add), .SUB(Command_Dekoder_sub), .zFlag(zFlag), .PCSel(PCSel), .PCLoad(PCLoad),
    .Write(Write), .InstructionLoad(InstructionLoad), .ImmediateLoad(ImmediateLoad), .RegWrite(RegWrite),
    .RegSel(RegSel), .dRegSel(dRegSel), .sRegSel(sRegSel), .opSel(opSel), .AddressSel(AddressSel));
endmodule

module CPU_Complete (
  output [7:0] DataInReg,
  output [7:0] AdresBus,
  output [7:0] Databus,
  output [7:0] dBus,
  output [7:0] sBus,
  output [7:0] Immediate,
  output [7:0] ALUOut,
  output [7:0] R1,
  output [7:0] R2,
  output [7:0] Zyklus
);

  wire Controller_immediateload, Controller_instructionload, Controller_pcload, Controller_pcsel,
       Controller_regwrite, Controller_write, RAM_ALU_zeroflag, Takt_out;
  wire [1:0] Controller_addresssel, Controller_dregsel, Controller_opsel, Controller_regsel,
       Controller_sregsel;
  wire [7:0] RAM_ALU_instruction;

  Clock Takt (.out(Takt_out));
  CPU_Controller Controller (
    .InstructionReg(RAM_ALU_instruction), .zFlag(RAM_ALU_zeroflag), .Takt(Takt_out),
    .PCSel(Controller_pcsel), .PCLoad(Controller_pcload), .Write(Controller_write),
    .InstructionLoad(Controller_instructionload), .ImmediateLoad(Controller_immediateload),
    .RegWrite(Controller_regwrite), .RegSel(Controller_regsel), .dRegSel(Controller_dregsel),
    .sRegSel(Controller_sregsel), .opSel(Controller_opsel), .AddressSel(Controller_addresssel),
    .Zyklus(Zyklus));
  RAM_ALU RAM_ALU (
    .PCSel(Controller_pcsel), .AddressSel(Controller_addresssel), .PCLoad(Controller_pcload),
    .Takt(Takt_out), .Write(Controller_write), .InstructionLoad(Controller_instructionload),
    .ImmediateLoad(Controller_immediateload), .RegWrite(Controller_regwrite), .RegSel(Controller_regsel),
    .dRegSel(Controller_dregsel), .sRegSel(Controller_sregsel), .opSel(Controller_opsel),
    .DataInReg(DataInReg), .AdressBus(AdresBus), .DataBus(Databus), .Instruction(RAM_ALU_instruction),
    .dBus(dBus), .sBus(sBus), .Immediate(Immediate), .ZeroFlag(RAM_ALU_zeroflag), .ALUout(ALUOut), .R1(R1),
    .R2(R2));  // open: NegativFlag, R3, R4
endmodule

module GatterErsatz (
  input  E,
  input  E1,
  input  E2,
  input  E1_2,
  input  E2_2,
  output A,
  output A_2,
  output A_3
);

  wire NAND_2_out, NAND_3_out, NAND_4_out;

  nand NAND (A, E, E);
  nand NAND_2 (NAND_2_out, E1, E2);
  nand NAND_3 (NAND_3_out, E1_2, E1_2);
  nand NAND_4 (NAND_4_out, E2_2, E2_2);
  nand NAND_5 (A_2, NAND_2_out, NAND_2_out);
  nand NAND_6 (A_3, NAND_3_out, NAND_4_out);

  // Notes on the sheet:
  //   NOT
  //   AND
  //   OR
endmodule
