# Fritzing sketch MyFlightControll (saved by Fritzing 0.9.3b)
breadboards: 1

parts:
  Bauteil1 = Arduino Nano (Rev3.0)
  BATT1 = LiPoly Battery (1300mAh)
  M2 = ESC
  920KV_Motor2 = DJI 920 KV Motor
  GY1 = MPU-6050 Board GY-521 [form="♀ (female)" package=THT]
  M3 = ESC
  920KV_Motor3 = DJI 920 KV Motor
  M4 = ESC
  920KV_Motor4 = DJI 920 KV Motor
  M5 = ESC
  920KV_Motor5 = DJI 920 KV Motor
  R1 = Resistor [tolerance=±5% resistance=330 package=THT]
  R2 = Resistor [tolerance=±5% resistance=1k package=THT]
  R3 = Resistor [tolerance=±5% resistance=1.5k package=THT]
  D1 = Diode [package=diode-1n4001]
  LED1 = smd LED [color="Red (633nm)" package="0603 [SMD]"]
  J2 = FS-IA6 [form="♂ (shrouded male)" package=THT]

nets:
  GND: Bauteil1.GND, BATT1.negative, M2.GND, GY1.pin2, M3.GND, M4.GND, M5.GND, R2.Pin_1, LED1.anode, J2.pin15
  N1: Bauteil1.D2, GY1.pin8
  N2: Bauteil1.D4, M2.DATA
  N3: Bauteil1.D5, M3.DATA
  N4: Bauteil1.D6, M4.DATA
  N5: Bauteil1.D7, M5.DATA
  N6: Bauteil1.D8, J2.pin13
  N7: Bauteil1.D9, J2.pin5
  N8: Bauteil1.D10, J2.pin4
  N9: Bauteil1.D11/MOSI, J2.pin3
  N10: Bauteil1.D12/MISO, R1.Pin_0
  N11: Bauteil1.VIN, R3.Pin_1, D1.C
  N12: Bauteil1.5V, GY1.pin1
  N13: Bauteil1.A5, GY1.pin3
  N14: Bauteil1.A4, GY1.pin4
  N15: Bauteil1.A0, R2.Pin_0, R3.Pin_0
  N16: BATT1.positive, D1.A, J2.pin12
  N17: M2.U, 920KV_Motor2.u
  N18: M2.V, 920KV_Motor2.v
  N19: M2.W, 920KV_Motor2.w
  N20: M3.U, 920KV_Motor3.u
  N21: M3.V, 920KV_Motor3.v
  N22: M3.W, 920KV_Motor3.w
  N23: M4.U, 920KV_Motor4.u
  N24: M4.V, 920KV_Motor4.v
  N25: M4.W, 920KV_Motor4.w
  N26: M5.U, 920KV_Motor5.u
  N27: M5.V, 920KV_Motor5.v
  N28: M5.W, 920KV_Motor5.w
  N29: R1.Pin_1, LED1.cathode

notes:
  M1 CCW
  M2 CW
  M3 CCW
  M4 CW

custom parts:
  LiPoly Battery (1300mAh): Lithium Ion Polymer Battery (1300mAh)
  DJI 920 KV Motor: DJI Brushless Outrunner 2212/920K Motor F330-550
  MPU-6050 Board GY-521: Acelerometro y Giroscopio MPU-6050 Board GY-521
  FS-IA6: FlySky FS-IA6 Receiver
